# Fritzing sketch MACROPAD-FRIT (saved by Fritzing 0.9.9b)
circuit board: 11.752cm x 8.37085cm

parts:
  RP2040 = Raspberry Pi Pico
  SW1 = Cherry MX Keyswitch Simple
  SW4 = Cherry MX Keyswitch Simple
  SW7 = Cherry MX Keyswitch Simple
  SW8 = Cherry MX Keyswitch Simple
  SW5 = Cherry MX Keyswitch Simple
  SW2 = Cherry MX Keyswitch Simple
  SW9 = Cherry MX Keyswitch Simple
  SW3 = Cherry MX Keyswitch Simple
  SW6 = Cherry MX Keyswitch Simple

nets:
  N1: RP2040.pin_22, SW9.pin_2
  N2: RP2040.pin_24, SW8.pin_2
  N3: RP2040.pin_25, SW7.pin_2
  N4: RP2040.pin_26, SW6.pin_2
  N5: RP2040.pin_27, SW5.pin_2
  N6: RP2040.pin_29, SW4.pin_2
  N7: RP2040.pin_31, SW3.pin_2
  N8: RP2040.pin_32, SW2.pin_2
  N9: RP2040.pin_34, SW1.pin_2
  N10: RP2040.pin_36, SW1.pin_1, SW4.pin_1, SW7.pin_1, SW8.pin_1, SW5.pin_1, SW2.pin_1, SW9.pin_1, SW3.pin_1, SW6.pin_1

custom parts:
  Raspberry Pi Pico: Raspberry Pi Pico. Based around the RP2040 microcontroller the Pico is a low cost microcontroller device bringing Raspberry Pi quality, cost, and easy of use to the microcontroller space. Jan 2021, Split part in to two versions: tht (this one) and SMD. This one will drill holes for a .1 in header in pcb to allow plugging in the module as well as providing pads to solder the module to the top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
  Cherry MX Keyswitch Simple: Cherry MX Keyswitch button for keyboards

// code stored in the sketch: CODE.ino
#include <Keyboard.h>


const int sw1 = 28;
const int sw2 = 27;
const int sw3 = 26;
const int sw4 = 22;
const int sw5 = 21;
const int sw6 = 20;
const int sw7 = 19;
const int sw8 = 18;
const int sw9 = 17;


//---------------------------------------------------------------------//
void setup(){ 
  Serial.begin(9600);
//-------------------//
  pinMode(sw1, INPUT);
  //-------------------//


}



//---------------------------------SI pin 1 recoit du courant alors faire actions----------------------------------//
void loop() {
 if (digitalRead(sw1) == HIGH) {
    actionsw1();
  }
  
  delay(100);


}


//--------------------------------Action réalisé dans le si------------------------------------//


void actionsw1() {
  
  Keyboard.begin();


  delay(2000);


  Keyboard.press(KEY_LEFT_CTRL);    
  Keyboard.press(KEY_LEFT_ALT);     
  Keyboard.press(KEY_DELETE);       
  
  delay(100);  
  
  Keyboard.releaseAll();


  Keyboard.end();
  
}
